# Fritzing sketch Esquema-PCB3 (saved by Fritzing 0.9.3b)
circuit board: 6.8456cm x 5.70472cm
breadboards: 1

parts:
  J2 = female pin header, 2 pins [form="♀ (female)"]
  M3 = DC Motor
  S2 = Toggle Switch [package=THT]
  J1 = female pin header, 2 pins [form="♀ (female)"]
  M4 = DC Motor
  Puente_Doble_H1 = Motor Driver 1A Dual TB6612FNG
  J3 = female pin header, 2 pins [form="♀ (female)"]
  S1 = Pushbutton [package="[THT]"]
  R1 = Resistor [tolerance=±5% resistance=220 package="2512 [SMD]"]
  VCC3 = Battery
  Arduino1 = Arduino Nano (Rev3.0)

nets:
  N1: J2.pin1, Arduino1.A1
  VCC: J2.pin2, J1.pin1, Puente_Doble_H1.VCC, S1.Pin_3, S1.Pin_4, Arduino1.5V
  N2: M3.pin_1, Puente_Doble_H1.B01
  N3: M3.pin_2, Puente_Doble_H1.B02
  N4: S2.COM, VCC3.+
  N5: S2.L2, Puente_Doble_H1.VM, Arduino1.VIN
  GND: J1.pin2, Puente_Doble_H1.GND, J3.pin1, R1.Pin_1, VCC3.-, Arduino1.GND
  N6: M4.pin_1, Puente_Doble_H1.A01
  N7: M4.pin_2, Puente_Doble_H1.A02
  N8: Puente_Doble_H1.PWMA, Arduino1.D6
  N9: Puente_Doble_H1.AIN2, Arduino1.D7
  N10: Puente_Doble_H1.AIN1, Arduino1.D8
  N11: Puente_Doble_H1.STBY, Arduino1.D9
  N12: Puente_Doble_H1.BIN1, Arduino1.D10
  N13: Puente_Doble_H1.BIN2, Arduino1.D11/MOSI
  N14: Puente_Doble_H1.PWMB, Arduino1.D12/MISO
  N15: J3.pin2, Arduino1.A0
  N16: S1.Pin_1, S1.Pin_2, R1.Pin_0, Arduino1.D2
