# Fritzing sketch Esquema-PCB-Regleta (saved by Fritzing 0.9.3b)
circuit board: 10cm x 4.5cm
breadboards: 1

parts:
  S3 = Pushbutton [package="[THT]"]
  S4 = Toggle Switch [package=THT]
  J4 = female pin header, 2 pins [form="♀ (female)"]
  J5 = female pin header, 2 pins [form="♀ (female)"]
  J6 = female pin header, 2 pins [form="♀ (female)"]
  Arduino2 = Arduino Nano (Rev3.0)
  Puente_Doble_H2 = Motor Driver 1A Dual TB6612FNG
  J7 = female pin header, 2 pins [form="♀ (female)"]
  TRM2 = Terminal 2pin
  TRM1 = Terminal 2pin
  TRM3 = Terminal 2pin
  R2 = Resistor [tolerance=±5% resistance=220 package="2512 [SMD]"]

nets:
  N1: S3.Pin_1, S3.Pin_2, Arduino2.D2, R2.Pin_0
  5V: S3.Pin_3, S3.Pin_4, J4.pin1, Arduino2.5V, Puente_Doble_H2.VCC
  N2: S4.COM, TRM3.pin_2
  N3: S4.L2, Arduino2.VIN, Puente_Doble_H2.VM
  GND: J4.pin2, Arduino2.GND, Puente_Doble_H2.GND, TRM3.pin_1, R2.Pin_1
  N4: J5.pin1, Arduino2.A4
  N5: J5.pin2, Arduino2.A3
  N6: J6.pin1, Arduino2.A2
  N7: J6.pin2, Arduino2.A1
  N8: Arduino2.D5, Puente_Doble_H2.PWMA
  N9: Arduino2.D6, Puente_Doble_H2.PWMB
  N10: Arduino2.D7, Puente_Doble_H2.AIN2
  N11: Arduino2.D8, Puente_Doble_H2.AIN1
  N12: Arduino2.D9, Puente_Doble_H2.STBY
  N13: Arduino2.D10, Puente_Doble_H2.BIN1
  N14: Arduino2.D11/MOSI, Puente_Doble_H2.BIN2
  N15: Arduino2.A0, J7.pin1
  N16: Puente_Doble_H2.B01, TRM2.pin_1
  N17: Puente_Doble_H2.B02, TRM2.pin_2
  N18: Puente_Doble_H2.A02, TRM1.pin_1
  N19: Puente_Doble_H2.A01, TRM1.pin_2

custom parts:
  Terminal 2pin: 2-pin Terminal Block
